// Digital circuit 4bit-bin-to-bcd.dig as structural Verilog
module _4bit_bin_to_bcd (
  input  [3:0] In,
  input  [3:0] Carry_in,
  output [3:0] Out,
  output [3:0] Carry
);

  ROM #(.AddrBits(5), .isProgramMemory("true"), .Bits(8)) rom_1 (.A({Carry_in[0], In}), .sel(1'b1), .D({Carry, Out}));
  // Pins of 1 and 4 bits meet at Carry_in

  // Notes on the sheet:
  //   In: 4-bit input representing a binary number to convert to BCD
  //   Out: 4-bit BCD output
  //   Carry: 4-bit carry from the BCD conversion
  //   Carry_in: Optional fifth bit to use for carry bit.
  //   contents of rom_1 (hex, n*v repeats v):
  //   0,1,2,3,4,5,6,7,8,9,10,11,12,13,14,15,16,17,18,19,20,21,22,23
  //   ,24,25,26,27,28,29,30,31
endmodule
