// Digital circuit cpsc111-intro.dig as structural Verilog
module cpsc111_intro (
  input  A,
  input  B,
  input  A_2,
  input  B_2,
  input  A_3,
  input  B_3,
  input  in_10,
  input  in_11,
  input  in_12,
  input  In,
  input  A_4,
  input  B_4,
  input  in_21,
  input  in_22,
  input  in_23,
  input  in_26,
  input  in_27,
  input  in_28,
  input  in_29,
  input  in_30,
  input  in_31,
  input  in_32,
  input  in_33,
  input  in_39,
  input  in_40,
  input  in_41,
  input  in_42,
  input  in_43,
  input  in_44,
  input  in_45,
  input  in_46,
  input  A_5,
  input  B_5,
  input  C_in,
  input  in_57,
  input  in_58,
  input  in_59,
  input  in_60,
  input  A_6,
  input  B_6,
  input  C_in_2,
  input  A_7,
  input  B_7,
  output out_1,
  output out_8,
  output out_9,
  output Out,
  output out_15,
  output out_18,
  output out_19,
  output out_20,
  output out_24,
  output out_25,
  output out_34,
  output out_35,
  output out_36,
  output out_37,
  output out_38,
  output out_47,
  output out_48,
  output out_49,
  output out_50,
  output out_51,
  output out_55,
  output out_56,
  output out_64,
  output out_65,
  output out_66,
  output out_69
);

  wire add_5_c_o, add_6_c_o, add_7_c_o, add_8_c_o, add_9_c_o, add_10_c_o, and_4_out, and_5_out, and_6_out,
       and_7_out, xor_4_out, xor_5_out;
  wire [3:0] _4bit_bin_to_bcd_1_p3, _4bit_bin_to_bcd_1_p4, _4bit_bin_to_bcd_2_p2, _4bit_bin_to_bcd_2_p3,
       _4bit_bin_to_bcd_3_p2, _4bit_bin_to_bcd_3_p3, _4bit_bin_to_bcd_4_p2, _4bit_bin_to_bcd_4_p3;

  and and_1 (out_1, A, B);
  or or_1 (out_8, A_2, B_2);
  xor xor_1 (out_9, A_3, B_3);
  Seven_Seg_Hex seven_seg_hex_1 (.d({in_57, 3'b000}), .dp(1'b0));
  Seven_Seg_Hex seven_seg_hex_2 (.d({1'b0, in_58, 2'b00}), .dp(1'b0));
  Seven_Seg_Hex seven_seg_hex_3 (.d({2'b00, in_59, 1'b0}), .dp(1'b0));
  Seven_Seg_Hex seven_seg_hex_4 (.d({3'b000, in_60}), .dp(1'b0));
  Seven_Seg_Hex seven_seg_hex_5 (.d(_4bit_bin_to_bcd_1_p4), .dp(1'b0));
  Seven_Seg_Hex seven_seg_hex_6 (.d(_4bit_bin_to_bcd_1_p3), .dp(1'b0));
  // _4bit_bin_to_bcd _4bit_bin_to_bcd_1: pin names not known; wires that end beside it: {in_57, in_58, in_59, in_60}, 1'b0, _4bit_bin_to_bcd_1_p3, _4bit_bin_to_bcd_1_p4
  xor xor_2 (out_18, A_4, B_4);
  and and_2 (out_15, A_4, B_4);
  xor xor_3 (out_69, A_7, B_7);
  and and_3 (out_66, A_7, B_7);
  Seven_Seg_Hex seven_seg_hex_7 (.d({2'b00, out_66, out_69}), .dp(1'b0));
  xor xor_4 (xor_4_out, A_5, B_5);
  and and_4 (and_4_out, A_5, B_5);
  xor xor_5 (xor_5_out, A_6, B_6);
  and and_5 (and_5_out, A_6, B_6);
  xor xor_6 (out_56, xor_4_out, C_in);
  and and_6 (and_6_out, xor_4_out, C_in);
  xor xor_7 (out_65, xor_5_out, C_in_2);
  and and_7 (and_7_out, xor_5_out, C_in_2);
  or or_2 (out_55, and_4_out, and_6_out);
  or or_3 (out_64, and_5_out, and_7_out);
  Seven_Seg_Hex seven_seg_hex_8 (.d({2'b00, out_64, out_65}), .dp(1'b0));
  Add add_1 (.a(in_22), .b(in_21), .c_i(in_23), .s(out_25), .c_o(out_24));
  Add add_2 (.a(in_11), .b(in_10), .c_i(in_12), .s(out_20), .c_o(out_19));
  Seven_Seg_Hex seven_seg_hex_9 (.d({2'b00, out_24, out_25}), .dp(1'b0));
  Add add_3 (.a(in_32), .b(in_28), .c_i(add_5_c_o), .s(out_37), .c_o(out_38));
  Add add_4 (.a(in_45), .b(in_41), .c_i(add_6_c_o), .s(out_50), .c_o(out_51));
  Add add_5 (.a(in_33), .b(in_29), .c_i(add_7_c_o), .s(out_36), .c_o(add_5_c_o));
  Add add_6 (.a(in_46), .b(in_42), .c_i(add_8_c_o), .s(out_49), .c_o(add_6_c_o));
  Add add_7 (.a(in_30), .b(in_26), .c_i(add_9_c_o), .s(out_35), .c_o(add_7_c_o));
  Add add_8 (.a(in_43), .b(in_39), .c_i(add_10_c_o), .s(out_48), .c_o(add_8_c_o));
  Add add_9 (.a(in_31), .b(in_27), .c_i(1'b0), .s(out_34), .c_o(add_9_c_o));
  Add add_10 (.a(in_44), .b(in_40), .c_i(1'b0), .s(out_47), .c_o(add_10_c_o));
  // _4bit_bin_to_bcd _4bit_bin_to_bcd_2: pin names not known; wires that end beside it: 1'b0, _4bit_bin_to_bcd_2_p2, _4bit_bin_to_bcd_2_p3
  // _4bit_bin_to_bcd _4bit_bin_to_bcd_3: pin names not known; wires that end beside it: 1'b0, _4bit_bin_to_bcd_3_p2, _4bit_bin_to_bcd_3_p3
  // _4bit_bin_to_bcd _4bit_bin_to_bcd_4: pin names not known; wires that end beside it: out_51, _4bit_bin_to_bcd_4_p2, _4bit_bin_to_bcd_4_p3
  Seven_Seg_Hex seven_seg_hex_10 (.d(_4bit_bin_to_bcd_2_p2), .dp(1'b0));
  Seven_Seg_Hex seven_seg_hex_11 (.d(_4bit_bin_to_bcd_2_p3), .dp(1'b0));
  Seven_Seg_Hex seven_seg_hex_12 (.d(_4bit_bin_to_bcd_3_p2), .dp(1'b0));
  Seven_Seg_Hex seven_seg_hex_13 (.d(_4bit_bin_to_bcd_3_p3), .dp(1'b0));
  Seven_Seg_Hex seven_seg_hex_14 (.d(_4bit_bin_to_bcd_4_p2), .dp(1'b0));
  Seven_Seg_Hex seven_seg_hex_15 (.d(_4bit_bin_to_bcd_4_p3), .dp(1'b0));

  assign Out = In;

  // Other names for the same wires on the sheet: _1A0 = in_60; _1A1 = in_59; _1A2 = in_58; _1A3 = in_57; _6A0 = in_44;
  //   _6A1 = in_43; _6A2 = in_46; _6A3 = in_45; _6B0 = in_40; _6B1 = in_39; _6B2 = in_42; _6B3 = in_41; _6S0 = out_47;
  //   _6S1 = out_48; _6S2 = out_49; _6S3 = out_50; _6SC = out_51

  // Notes on the sheet:
  //   Boolean Values
  //   Only two possible values:
  //   T or F
  //   1 or 0
  //   ON or OFF
  //   Boolean Logic
  //   AND
  //   OR
  //   XOR
  //   3
  //   +
  //   Binary Numbers
  //   2
  //   1
  //   0
  //   =
  //   Half Adder
  //   Result
  //   Full Adder
  //   Carry
  //   Sum
  //   Full Adder (Packaged)
  //   A
  //   B
  //   C_in
  //   C_out
  //   S
  //   S_3
  //   4-bit Adder
  //   S_2
  //   S_1
  //   S_0
endmodule
